// Logisim project riscv32 bit single cycle  processor logisim.circ as structural Verilog: 11 circuits, main circuit ALL
// signal controller
module signal_controler (
  input  r,
  input  i,
  input  s,
  input  lui,
  input  auipc,
  input  jal,
  input  branch_true,
  input  b,
  input  jalr,
  input  lw,
  output out_11,
  output [1:0] op_A,
  output op_B,
  output mem_write,
  output mem_read,
  output [1:0] imm_sel,
  output write_back,
  output reg_file,
  output [1:0] PC_sel,
  output jalr_2,
  output [2:0] alu_op_2_1_0
);

  wire cond_cheak_out;

  and cond_cheak (cond_cheak_out, branch_true, b);
  or or_1 (op_B, i, s, lui, auipc, jalr, lw);
  or or_2 (imm_sel[0], jal, cond_cheak_out, s, r);
  or or_3 (imm_sel[1], auipc, lui, jal, cond_cheak_out, r);
  or or_4 (reg_file, r, i, jal, lui, auipc, jalr, lw);
  or or_5 (PC_sel[0], jalr, cond_cheak_out);
  or or_6 (PC_sel[1], jal, jalr);
  or or_7 (op_A[0], r, jalr, lui, lw, i, s);
  or or_8 (out_11, s, b);
  or or_9 (op_A[1], lui, auipc);
  ALUop2_1_0 aluop2_1_0_1 (
    .r(r), .I(i), .s(s), .Lui(lui), .Auipc(auipc), .Jal(jal), .Jalr(jalr), .Lw(lw), .out_9(alu_op_2_1_0));

  assign jalr_2 = jalr;
  assign mem_read = lw;
  assign mem_write = s;
  assign write_back = lw;
endmodule

module type_decorder (
  input  [6:0] in_1,
  input  in_2,
  output r,
  output i,
  output s,
  output lui,
  output auipc,
  output jal,
  output branch_true,
  output b,
  output jalr,
  output lw
);

  Comparator #(.width(7)) comparator_1 (.a(in_1), .b(7'b0110011), .eq(r));  // open: gt, lt
  Comparator #(.width(7)) comparator_2 (.a(in_1), .b(7'b0010011), .eq(i));  // open: gt, lt
  Comparator #(.width(7)) comparator_3 (.a(in_1), .b(7'b0100011), .eq(s));  // open: gt, lt
  Comparator #(.width(7)) comparator_4 (.a(in_1), .b(7'b0110111), .eq(lui));  // open: gt, lt
  Comparator #(.width(7)) comparator_5 (.a(in_1), .b(7'b0010111), .eq(auipc));  // open: gt, lt
  Comparator #(.width(7)) comparator_6 (.a(in_1), .b(7'b1101111), .eq(jal));  // open: gt, lt
  Comparator #(.width(7)) comparator_7 (.a(in_1), .b(7'b1100011), .eq(b));  // open: gt, lt
  Comparator #(.width(7)) comparator_8 (.a(in_1), .b(7'b1100111), .eq(jalr));  // open: gt, lt
  Comparator #(.width(7)) comparator_9 (.a(in_1), .b(7'b0000011), .eq(lw));  // open: gt, lt

  assign branch_true = in_2;
endmodule

// opcode to signals
module signal_controller_and_type_decorder (
  input  [6:0] in_1,
  input  in_2,
  output b___s,
  output [1:0] op_A,
  output op_B,
  output mem_write,
  output mem_read,
  output [1:0] imm_sel,
  output write_back,
  output reg_file,
  output [1:0] PC_sel,
  output JALR,
  output [2:0] alu_op_2_1_0
);

  wire type_decorder_1_auipc, type_decorder_1_b, type_decorder_1_branch_true, type_decorder_1_i,
       type_decorder_1_jal, type_decorder_1_jalr, type_decorder_1_lui, type_decorder_1_lw, type_decorder_1_r,
       type_decorder_1_s;

  type_decorder type_decorder_1 (
    .in_1(in_1), .r(type_decorder_1_r), .i(type_decorder_1_i), .s(type_decorder_1_s),
    .lui(type_decorder_1_lui), .auipc(type_decorder_1_auipc), .jal(type_decorder_1_jal),
    .b(type_decorder_1_b), .jalr(type_decorder_1_jalr), .lw(type_decorder_1_lw),
    .branch_true(type_decorder_1_branch_true), .in_2(in_2));
  signal_controler signal_controler_1 (
    .r(type_decorder_1_r), .i(type_decorder_1_i), .s(type_decorder_1_s), .lui(type_decorder_1_lui),
    .auipc(type_decorder_1_auipc), .jal(type_decorder_1_jal), .b(type_decorder_1_b),
    .jalr(type_decorder_1_jalr), .lw(type_decorder_1_lw), .op_A(op_A), .op_B(op_B), .mem_write(mem_write),
    .mem_read(mem_read), .imm_sel(imm_sel), .write_back(write_back), .reg_file(reg_file), .PC_sel(PC_sel),
    .alu_op_2_1_0(alu_op_2_1_0), .branch_true(type_decorder_1_branch_true), .jalr_2(JALR), .out_11(b___s));
endmodule

// ALU
module alu (
  input  [31:0] a,
  input  [31:0] b,
  input  [3:0] in_3,
  output [31:0] out_4
);

  wire comparator_1_lt, comparator_2_lt;
  wire [31:0] adder_1_out, and_1_out, bit_extender_1_out, bit_extender_2_out, or_1_out, shifter_1_out,
       shifter_2_out, shifter_3_out, subtractor_1_out, xor_1_out;

  Adder #(.width(32)) adder_1 (.a(a), .b(b), .out(adder_1_out), .cin(1'b0));  // open: cout
  Subtractor #(.width(32)) subtractor_1 (.a(a), .b(b), .out(subtractor_1_out), .bin(1'b0));  // open: bout
  assign and_1_out = a & b;  // AND_Gate and_1, 32 bits wide
  assign or_1_out = a | b;  // OR_Gate or_1, 32 bits wide
  assign xor_1_out = a ^ b;  // XOR_Gate xor_1, 32 bits wide
  Shifter #(.width(32)) shifter_1 (.in(a), .\dist (b[4:0]), .out(shifter_1_out));
  Shifter #(.width(32), .shift("lr")) shifter_2 (.in(a), .\dist (b[4:0]), .out(shifter_2_out));
  Shifter #(.width(32), .shift("ar")) shifter_3 (.in(a), .\dist (b[4:0]), .out(shifter_3_out));
  Comparator #(.width(32)) comparator_1 (.a(a), .b(b), .lt(comparator_1_lt));  // open: gt, eq
  Comparator #(.width(32), .mode("unsigned")) comparator_2 (.a(a), .b(b), .lt(comparator_2_lt));  // open: gt, eq
  assign bit_extender_1_out = {{31{comparator_1_lt}}, comparator_1_lt};  // Bit_Extender bit_extender_1
  assign bit_extender_2_out = {{31{comparator_2_lt}}, comparator_2_lt};  // Bit_Extender bit_extender_2
  Multiplexer #(.select(4), .width(32)) multiplexer_1 (
    .in0(adder_1_out), .in1(subtractor_1_out), .in2(and_1_out), .in3(or_1_out), .in4(xor_1_out),
    .in5(shifter_2_out), .in6(shifter_3_out), .in7(shifter_1_out), .in8(bit_extender_1_out),
    .in9(bit_extender_2_out), .in14(b), .in15(a), .out(out_4), .sel(in_3));  // open: in10, in11, in12, in13, en
endmodule

// FETCH
module ALL (
  input  reset,
  output [4:0] rs1,
  output [4:0] rs2,
  output [4:0] out_4,
  output [9:0] out_5,
  output [1:0] op_A,
  output [31:0] out_7,
  output [31:0] out_8,
  output [31:0] out_9,
  output [31:0] out_10
);

  wire branch_alu_1_out_4, clock_out, signal_controller_and_type_decorder_1_b___s,
       signal_controller_and_type_decorder_1_jalr, signal_controller_and_type_decorder_1_mem_read,
       signal_controller_and_type_decorder_1_mem_write, signal_controller_and_type_decorder_1_op_b,
       signal_controller_and_type_decorder_1_reg_file, signal_controller_and_type_decorder_1_write_back;
  wire [1:0] signal_controller_and_type_decorder_1_imm_sel, signal_controller_and_type_decorder_1_pc_sel;
  wire [2:0] rom_1_data_2, signal_controller_and_type_decorder_1_alu_op_2_1_0;
  wire [3:0] alu_controller_1_out_4;
  wire [9:0] register_1_q_2;
  wire [31:0] adder_1_out, alu_1_out_4, imm_gen_1_b, imm_gen_1_j, imm_gen_1_out_4, multiplexer_1_out,
       multiplexer_2_out, multiplexer_3_out, multiplexer_4_out, multiplexer_5_out, register_1_q, rom_1_data;

  Multiplexer #(.select(2), .width(32)) multiplexer_1 (
    .in0(adder_1_out), .in1(imm_gen_1_b), .in2(imm_gen_1_j),
    .in3({alu_1_out_4[31:12], out_5, alu_1_out_4[1:0]}), .out(multiplexer_1_out),
    .sel(signal_controller_and_type_decorder_1_pc_sel));  // open: en
  Register #(.width(32)) register_1 (
    .D(multiplexer_1_out), .Q({register_1_q[31:12], register_1_q_2, register_1_q[1:0]}), .clk(clock_out),
    .clr(reset));  // open: en
  Adder #(.width(32)) adder_1 (
    .a({register_1_q[31:12], register_1_q_2, register_1_q[1:0]}), .b(32'h4), .out(adder_1_out), .cin(1'b0));  // open: cout
  ROM #(.addrWidth(10), .dataWidth(32)) rom_1 (
    .addr(register_1_q_2), .data({rom_1_data[31:25], rs2, rs1, rom_1_data_2, out_4, rom_1_data[6:0]}));  // open: sel
  Clock clock (.out(clock_out));
  IMM_gen imm_gen_1 (
    .in_1({rom_1_data[31:25], rs2, rs1, rom_1_data_2, out_4, rom_1_data[6:0]}), .out_4(imm_gen_1_out_4),
    .in_2(signal_controller_and_type_decorder_1_imm_sel),
    .mem({register_1_q[31:12], register_1_q_2, register_1_q[1:0]}), .j(imm_gen_1_j), .b(imm_gen_1_b));
  signal_controller_and_type_decorder signal_controller_and_type_decorder_1 (
    .in_1(rom_1_data[6:0]), .op_A(op_A), .op_B(signal_controller_and_type_decorder_1_op_b),
    .mem_write(signal_controller_and_type_decorder_1_mem_write),
    .mem_read(signal_controller_and_type_decorder_1_mem_read),
    .imm_sel(signal_controller_and_type_decorder_1_imm_sel),
    .write_back(signal_controller_and_type_decorder_1_write_back),
    .reg_file(signal_controller_and_type_decorder_1_reg_file),
    .PC_sel(signal_controller_and_type_decorder_1_pc_sel), .JALR(signal_controller_and_type_decorder_1_jalr),
    .alu_op_2_1_0(signal_controller_and_type_decorder_1_alu_op_2_1_0), .in_2(branch_alu_1_out_4),
    .b___s(signal_controller_and_type_decorder_1_b___s));
  reg_file reg_file_1 (
    .rs1(rs1), .rs2(rs2), .r_sel(out_4), .rs2__D(out_10), .rs1_D(out_8), .reset(reset), .clock(clock_out),
    .reg_file_en(signal_controller_and_type_decorder_1_reg_file), .in_1(out_9));
  alu_controller alu_controller_1 (
    .func7(rom_1_data[30]), .out_4(alu_controller_1_out_4),
    .aluop_2_1_0(signal_controller_and_type_decorder_1_alu_op_2_1_0), .func_2_1_0(rom_1_data_2));
  Multiplexer #(.select(2), .width(32)) multiplexer_2 (
    .in0(adder_1_out), .in1(out_8), .in2({register_1_q[31:12], register_1_q_2, register_1_q[1:0]}),
    .out(multiplexer_2_out), .sel(op_A));  // open: in3, en
  Multiplexer #(.width(32)) multiplexer_3 (
    .in0(out_10), .in1(imm_gen_1_out_4), .out(multiplexer_3_out),
    .sel(signal_controller_and_type_decorder_1_op_b));  // open: en
  branch_ALU branch_alu_1 (.rs1(out_8), .rs2(out_10), .bgeu_111(rom_1_data_2), .out_4(branch_alu_1_out_4));
  alu alu_1 (
    .a(multiplexer_2_out), .b(multiplexer_3_out), .in_3(alu_controller_1_out_4),
    .out_4({alu_1_out_4[31:12], out_5, alu_1_out_4[1:0]}));
  RAM #(.addrWidth(10), .dataWidth(32), .bus("separate")) ram_1 (
    .addr(out_5), .din(out_10), .data(out_7), .str(signal_controller_and_type_decorder_1_mem_write),
    .clk(clock_out), .ld(signal_controller_and_type_decorder_1_mem_read), .clr(reset));  // open: sel
  Multiplexer #(.width(32), .enable("false")) multiplexer_4 (
    .in0({alu_1_out_4[31:12], out_5, alu_1_out_4[1:0]}), .in1(out_7), .out(multiplexer_4_out),
    .sel(signal_controller_and_type_decorder_1_write_back));
  Multiplexer #(.width(32), .enable("false")) multiplexer_5 (
    .in0(multiplexer_4_out), .in1(adder_1_out), .out(multiplexer_5_out),
    .sel(signal_controller_and_type_decorder_1_jalr));
  Multiplexer #(.width(32), .enable("false")) multiplexer_6 (
    .in0(multiplexer_5_out), .out(out_9), .sel(signal_controller_and_type_decorder_1_b___s));  // open: in1

  // Notes on the sheet:
  //   01 B
  //   10 JAL
  //   11 JALR
  //   pc sel
  //   contents of rom_1 (hex, n*v repeats v):
  //   100093 100133 202223 402183
  //   b out
  //   pc
  //   imm sel
  //   i/s/u
  //   JAL
  //   BRANCH
  //   op A
  //   op B
  //   MEM write
  //   MEM read
  //   IMM sel
  //   pc sel
  //   jalr
  //   alo op
  //   write back
  //   reg file en
  //   rsel
  //   pc + 4
  //   rs1
  //   PC
  //   RS2
  //   imm
  //   op B
  //   b out
  //   func 3
  //   alu func
  //   pc+4
  //   wb sel
  //   rd
  //   JALR 
  //   b/s
endmodule

// imm gen
module IMM_gen (
  input  [31:0] in_1,
  input  [1:0] in_2,
  input  [31:0] mem,
  output [31:0] out_4,
  output [31:0] j,
  output [31:0] b
);

  wire [19:0] bit_extender_1_out;
  wire [31:0] shifter_1_out;

  assign bit_extender_1_out = {{19{1'b0}}, in_1[31]};  // Bit_Extender bit_extender_1
  Shifter #(.width(32)) shifter_1 (
    .in({bit_extender_1_out[11:0], in_1[31:12]}), .\dist (5'b01100), .out(shifter_1_out));
  Multiplexer #(.select(2), .width(32)) multiplexer_1 (
    .in0({bit_extender_1_out, in_1[31:20]}), .in1({bit_extender_1_out, in_1[31:25], in_1[11:7]}),
    .in2(shifter_1_out), .out(out_4), .sel(in_2));  // open: in3, en
  Adder #(.width(32)) adder_1 (
    .a({bit_extender_1_out[10:0], in_1[31], in_1[19:12], in_1[20], in_1[30:21], 1'b0}), .b(mem), .out(j),
    .cin(1'b0));  // open: cout
  Adder #(.width(32)) adder_2 (
    .a({bit_extender_1_out[18:0], in_1[31], in_1[7], in_1[30:25], in_1[11:8], 1'b0}), .b(mem), .out(b),
    .cin(1'b0));  // open: cout
endmodule

module reg_file (
  input  [31:0] in_1,
  input  [4:0] rs1,
  input  [4:0] rs2,
  input  reg_file_en,
  input  [4:0] r_sel,
  input  reset,
  input  clock,
  output [31:0] rs1_D,
  output [31:0] rs2__D
);

  wire decoder_1_out0, decoder_1_out1, decoder_1_out2, decoder_1_out3, decoder_1_out4, decoder_1_out5,
       decoder_1_out6, decoder_1_out7, decoder_1_out8, decoder_1_out9, decoder_1_out10, decoder_1_out11,
       decoder_1_out12, decoder_1_out13, decoder_1_out14, decoder_1_out15, decoder_1_out16, decoder_1_out17,
       decoder_1_out18, decoder_1_out19, decoder_1_out20, decoder_1_out21, decoder_1_out22, decoder_1_out23,
       decoder_1_out24, decoder_1_out25, decoder_1_out26, decoder_1_out27, decoder_1_out28, decoder_1_out29,
       decoder_1_out30, decoder_1_out31;
  wire [31:0] register_1_q, register_2_q, register_3_q, register_4_q, register_5_q, register_6_q,
       register_7_q, register_8_q, register_9_q, register_10_q, register_11_q, register_12_q, register_13_q,
       register_14_q, register_15_q, register_16_q, register_17_q, register_18_q, register_19_q,
       register_20_q, register_21_q, register_22_q, register_23_q, register_24_q, register_25_q,
       register_26_q, register_27_q, register_28_q, register_29_q, register_30_q, register_31_q,
       register_32_q;

  Decoder #(.select(5)) decoder_1 (
    .out0(decoder_1_out0), .out1(decoder_1_out1), .out2(decoder_1_out2), .out3(decoder_1_out3),
    .out4(decoder_1_out4), .out5(decoder_1_out5), .out6(decoder_1_out6), .out7(decoder_1_out7),
    .out8(decoder_1_out8), .out9(decoder_1_out9), .out10(decoder_1_out10), .out11(decoder_1_out11),
    .out12(decoder_1_out12), .out13(decoder_1_out13), .out14(decoder_1_out14), .out15(decoder_1_out15),
    .out16(decoder_1_out16), .out17(decoder_1_out17), .out18(decoder_1_out18), .out19(decoder_1_out19),
    .out20(decoder_1_out20), .out21(decoder_1_out21), .out22(decoder_1_out22), .out23(decoder_1_out23),
    .out24(decoder_1_out24), .out25(decoder_1_out25), .out26(decoder_1_out26), .out27(decoder_1_out27),
    .out28(decoder_1_out28), .out29(decoder_1_out29), .out30(decoder_1_out30), .out31(decoder_1_out31),
    .sel(r_sel), .en(reg_file_en));
  Register #(.width(32)) register_1 (.en(decoder_1_out0), .Q(register_1_q), .clk(clock), .clr(reset));  // open: D
  Register #(.width(32)) register_2 (.D(in_1), .en(decoder_1_out1), .Q(register_2_q), .clk(clock), .clr(reset));
  Register #(.width(32)) register_3 (.D(in_1), .en(decoder_1_out2), .Q(register_3_q), .clk(clock), .clr(reset));
  Register #(.width(32)) register_4 (.D(in_1), .en(decoder_1_out3), .Q(register_4_q), .clk(clock), .clr(reset));
  Register #(.width(32)) register_5 (.D(in_1), .en(decoder_1_out4), .Q(register_5_q), .clk(clock), .clr(reset));
  Register #(.width(32)) register_6 (.D(in_1), .en(decoder_1_out5), .Q(register_6_q), .clk(clock), .clr(reset));
  Register #(.width(32)) register_7 (.D(in_1), .en(decoder_1_out6), .Q(register_7_q), .clk(clock), .clr(reset));
  Register #(.width(32)) register_8 (.D(in_1), .en(decoder_1_out7), .Q(register_8_q), .clk(clock), .clr(reset));
  Register #(.width(32)) register_9 (.D(in_1), .en(decoder_1_out8), .Q(register_9_q), .clk(clock), .clr(reset));
  Register #(.width(32)) register_10 (.D(in_1), .en(decoder_1_out9), .Q(register_10_q), .clk(clock), .clr(reset));
  Register #(.width(32)) register_11 (.D(in_1), .en(decoder_1_out10), .Q(register_11_q), .clk(clock), .clr(reset));
  Register #(.width(32)) register_12 (.D(in_1), .en(decoder_1_out11), .Q(register_12_q), .clk(clock), .clr(reset));
  Register #(.width(32)) register_13 (.D(in_1), .en(decoder_1_out12), .Q(register_13_q), .clk(clock), .clr(reset));
  Register #(.width(32)) register_14 (.D(in_1), .en(decoder_1_out13), .Q(register_14_q), .clk(clock), .clr(reset));
  Register #(.width(32)) register_15 (.D(in_1), .en(decoder_1_out14), .Q(register_15_q), .clk(clock), .clr(reset));
  Register #(.width(32)) register_16 (.D(in_1), .en(decoder_1_out15), .Q(register_16_q), .clk(clock), .clr(reset));
  Register #(.width(32)) register_17 (.D(in_1), .en(decoder_1_out16), .Q(register_17_q), .clk(clock), .clr(reset));
  Register #(.width(32)) register_18 (.D(in_1), .en(decoder_1_out17), .Q(register_18_q), .clk(clock), .clr(reset));
  Register #(.width(32)) register_19 (.D(in_1), .en(decoder_1_out18), .Q(register_19_q), .clk(clock), .clr(reset));
  Register #(.width(32)) register_20 (.D(in_1), .en(decoder_1_out19), .Q(register_20_q), .clk(clock), .clr(reset));
  Register #(.width(32)) register_21 (.D(in_1), .en(decoder_1_out20), .Q(register_21_q), .clk(clock), .clr(reset));
  Register #(.width(32)) register_22 (.D(in_1), .en(decoder_1_out21), .Q(register_22_q), .clk(clock), .clr(reset));
  Register #(.width(32)) register_23 (.D(in_1), .en(decoder_1_out22), .Q(register_23_q), .clk(clock), .clr(reset));
  Register #(.width(32)) register_24 (.D(in_1), .en(decoder_1_out23), .Q(register_24_q), .clk(clock), .clr(reset));
  Register #(.width(32)) register_25 (.D(in_1), .en(decoder_1_out24), .Q(register_25_q), .clk(clock), .clr(reset));
  Register #(.width(32)) register_26 (.D(in_1), .en(decoder_1_out25), .Q(register_26_q), .clk(clock), .clr(reset));
  Register #(.width(32)) register_27 (.D(in_1), .en(decoder_1_out26), .Q(register_27_q), .clk(clock), .clr(reset));
  Register #(.width(32)) register_28 (.D(in_1), .en(decoder_1_out27), .Q(register_28_q), .clk(clock), .clr(reset));
  Register #(.width(32)) register_29 (.D(in_1), .en(decoder_1_out28), .Q(register_29_q), .clk(clock), .clr(reset));
  Register #(.width(32)) register_30 (.D(in_1), .en(decoder_1_out29), .Q(register_30_q), .clk(clock), .clr(reset));
  Register #(.width(32)) register_31 (.D(in_1), .en(decoder_1_out30), .Q(register_31_q), .clk(clock), .clr(reset));
  Register #(.width(32)) register_32 (.D(in_1), .en(decoder_1_out31), .Q(register_32_q), .clk(clock), .clr(reset));
  Multiplexer #(.select(5), .width(32), .enable("false")) multiplexer_1 (
    .in0(register_1_q), .in1(register_2_q), .in2(register_3_q), .in3(register_4_q), .in4(register_5_q),
    .in5(register_6_q), .in6(register_7_q), .in7(register_8_q), .in8(register_9_q), .in9(register_10_q),
    .in10(register_11_q), .in11(register_12_q), .in12(register_13_q), .in13(register_14_q),
    .in14(register_15_q), .in15(register_16_q), .in16(register_17_q), .in17(register_18_q),
    .in18(register_19_q), .in19(register_20_q), .in20(register_21_q), .in21(register_22_q),
    .in22(register_23_q), .in23(register_24_q), .in24(register_25_q), .in25(register_26_q),
    .in26(register_27_q), .in27(register_28_q), .in28(register_29_q), .in29(register_30_q),
    .in30(register_31_q), .in31(register_32_q), .out(rs1_D), .sel(rs1));
  Multiplexer #(.select(5), .width(32), .enable("false")) multiplexer_2 (
    .in0(register_1_q), .in1(register_2_q), .in2(register_3_q), .in3(register_4_q), .in4(register_5_q),
    .in5(register_6_q), .in6(register_7_q), .in7(register_8_q), .in8(register_9_q), .in9(register_10_q),
    .in10(register_11_q), .in11(register_12_q), .in12(register_13_q), .in13(register_14_q),
    .in14(register_15_q), .in15(register_16_q), .in16(register_17_q), .in17(register_18_q),
    .in18(register_19_q), .in19(register_20_q), .in20(register_21_q), .in21(register_22_q),
    .in22(register_23_q), .in23(register_24_q), .in24(register_25_q), .in25(register_26_q),
    .in26(register_27_q), .in27(register_28_q), .in28(register_29_q), .in29(register_30_q),
    .in30(register_31_q), .in31(register_32_q), .out(rs2__D), .sel(rs2));
endmodule

module alu_controller (
  input  [2:0] aluop_2_1_0,
  input  [2:0] func_2_1_0,
  input  func7,
  output [3:0] out_4
);

  wire and_1_out, and_2_out, and_3_out, and_4_out, and_5_out, and_6_out, and_7_out, and_8_out, and_9_out,
       and_10_out, and_11_out, and_12_out, and_13_out, and_14_out, and_15_out, and_16_out, and_17_out,
       and_18_out, and_19_out, and_20_out, not_1_out, not_2_out, not_3_out, not_4_out, not_5_out, not_6_out,
       not_7_out, not_8_out, not_9_out, not_10_out, not_11_out, not_12_out, or_1_out, or_2_out, or_5_out,
       or_6_out, or_7_out, or_8_out;

  not not_1 (not_1_out, aluop_2_1_0[2]);
  not not_2 (not_2_out, aluop_2_1_0[0]);
  not not_3 (not_3_out, func_2_1_0[2]);
  not not_4 (not_4_out, func_2_1_0[1]);
  not not_5 (not_5_out, func_2_1_0[1]);
  not not_6 (not_6_out, func_2_1_0[2]);
  not not_7 (not_7_out, func_2_1_0[1]);
  not not_8 (not_8_out, func_2_1_0[2]);
  not not_9 (not_9_out, func_2_1_0[2]);
  not not_10 (not_10_out, func_2_1_0[1]);
  and and_1 (and_1_out, not_1_out, not_2_out);
  and and_2 (and_2_out, not_3_out, func_2_1_0[1]);
  and and_3 (and_3_out, not_4_out, func_2_1_0[0]);
  and and_4 (and_4_out, func_2_1_0[2], not_5_out);
  and and_5 (and_5_out, not_6_out, not_7_out);
  and and_6 (and_6_out, not_8_out, func7);
  and and_7 (and_7_out, not_9_out, func_2_1_0[0]);
  and and_8 (and_8_out, not_10_out, func_2_1_0[0]);
  not not_11 (not_11_out, func7);
  and and_9 (and_9_out, func_2_1_0[2], func_2_1_0[1]);
  not not_12 (not_12_out, func_2_1_0[0]);
  and and_10 (and_10_out, aluop_2_1_0[2], aluop_2_1_0[1]);
  and and_11 (and_11_out, and_1_out, and_2_out);
  and and_12 (and_12_out, aluop_2_1_0[2], aluop_2_1_0[1]);
  or or_1 (or_1_out, and_3_out, and_4_out);
  and and_13 (and_13_out, aluop_2_1_0[2], aluop_2_1_0[1]);
  and and_14 (and_14_out, and_5_out, func_2_1_0[0]);
  and and_15 (and_15_out, func_2_1_0[2], func7);
  and and_16 (and_16_out, func_2_1_0[2], func_2_1_0[1]);
  and and_17 (and_17_out, aluop_2_1_0[2], aluop_2_1_0[1]);
  or or_2 (or_2_out, and_6_out, and_7_out);
  and and_18 (and_18_out, and_8_out, not_11_out);
  and and_19 (and_19_out, and_9_out, not_12_out);
  and and_20 (and_20_out, and_10_out, aluop_2_1_0[0]);
  or or_3 (out_4[3], and_11_out, and_12_out);
  or or_4 (out_4[2], or_1_out, and_13_out);
  or or_5 (or_5_out, and_14_out, and_15_out);
  or or_6 (or_6_out, and_16_out, and_17_out);
  or or_7 (or_7_out, or_2_out, and_18_out);
  or or_8 (or_8_out, and_19_out, and_20_out);
  or or_9 (out_4[1], or_5_out, or_6_out);
  or or_10 (out_4[0], or_7_out, or_8_out);
endmodule

module branch_ALU (
  input  [31:0] rs1,
  input  [31:0] rs2,
  input  [2:0] bgeu_111,
  output out_4
);

  wire comparator_1_eq, comparator_1_gt, comparator_1_lt, comparator_2_eq, comparator_2_gt, comparator_2_lt,
       not_1_out, or_1_out, or_2_out;

  Comparator #(.width(32)) comparator_1 (
    .a(rs1), .b(rs2), .gt(comparator_1_gt), .eq(comparator_1_eq), .lt(comparator_1_lt));
  or or_1 (or_1_out, comparator_1_gt, comparator_1_eq);
  Comparator #(.width(32)) comparator_2 (
    .a(rs1), .b(rs2), .gt(comparator_2_gt), .eq(comparator_2_eq), .lt(comparator_2_lt));
  or or_2 (or_2_out, comparator_2_eq, comparator_2_gt);
  not not_1 (not_1_out, comparator_1_eq);
  Multiplexer #(.select(3)) multiplexer_1 (
    .in0(comparator_1_eq), .in1(not_1_out), .in4(comparator_1_lt), .in5(or_1_out), .in6(comparator_2_lt),
    .in7(or_2_out), .out(out_4), .sel(bgeu_111));  // open: in2, in3, en

  // Notes on the sheet:
  //   beq 000
  //   bne 001
  //   blt 100
  //   bge 101
  //   bltu 110
endmodule

module ALUop2_1_0 (
  input  r,
  input  I,
  input  s,
  input  Lui,
  input  Auipc,
  input  Jal,
  input  Jalr,
  input  Lw,
  output [2:0] out_9
);

  wire nand_1_out, nand_2_out, nand_3_out, nand_4_out, nand_5_out, nand_6_out, nand_7_out, nand_8_out,
       nand_9_out, nand_10_out, nand_11_out, nand_12_out, nand_13_out, nand_14_out, nand_15_out, nand_16_out,
       nand_17_out, nand_18_out, nand_19_out, nand_20_out, nand_21_out, nand_22_out, nand_23_out,
       nand_24_out, nand_25_out, nand_26_out, nand_27_out;

  nand nand_1 (nand_1_out, r, r);
  nand nand_2 (nand_2_out, I, I);
  nand nand_3 (nand_3_out, Jalr, Jalr);
  nand nand_4 (nand_4_out, Lw, Lw);
  nand nand_5 (nand_5_out, r, r);
  nand nand_6 (nand_6_out, s, s);
  nand nand_7 (nand_7_out, Auipc, Auipc);
  nand nand_8 (nand_8_out, Lw, Lw);
  nand nand_9 (nand_9_out, r, r);
  nand nand_10 (nand_10_out, I, I);
  nand nand_11 (nand_11_out, s, s);
  nand nand_12 (nand_12_out, Lui, Lui);
  nand nand_13 (nand_13_out, nand_1_out, nand_2_out);
  nand nand_14 (nand_14_out, nand_3_out, nand_4_out);
  nand nand_15 (nand_15_out, nand_5_out, nand_6_out);
  nand nand_16 (nand_16_out, nand_7_out, nand_8_out);
  nand nand_17 (nand_17_out, nand_9_out, nand_10_out);
  nand nand_18 (nand_18_out, nand_11_out, nand_12_out);
  nand nand_19 (nand_19_out, nand_13_out, nand_13_out);
  nand nand_20 (nand_20_out, nand_14_out, nand_14_out);
  nand nand_21 (nand_21_out, nand_15_out, nand_15_out);
  nand nand_22 (nand_22_out, nand_16_out, nand_16_out);
  nand nand_23 (nand_23_out, nand_17_out, nand_17_out);
  nand nand_24 (nand_24_out, nand_18_out, nand_18_out);
  nand nand_25 (nand_25_out, nand_19_out, nand_20_out);
  nand nand_26 (nand_26_out, nand_21_out, nand_22_out);
  nand nand_27 (nand_27_out, nand_23_out, nand_24_out);
  nand nand_28 (out_9[2], nand_25_out, nand_25_out);
  nand nand_29 (out_9[1], nand_26_out, nand_26_out);
  nand nand_30 (out_9[0], nand_27_out, nand_27_out);
endmodule

module dfh (
  input  r,
  input  I,
  input  s,
  input  Lui,
  input  Auipc,
  input  Jal,
  input  Jalr,
  input  Lw,
  output [2:0] op_2_1_0
);

  ALUop2_1_0 aluop2_1_0_1 (
    .r(r), .I(I), .s(s), .Lui(Lui), .Auipc(Auipc), .Jal(Jal), .Jalr(Jalr), .Lw(Lw), .out_9(op_2_1_0));
  branch_ALU branch_alu_1 ();  // open: rs1, rs2, bgeu_111, out_4
endmodule
