// Logisim project single cycle piplined.circ as structural Verilog: 16 circuits, main circuit ALL
// signal controller
module signal_controler (
  input  r,
  input  i,
  input  s,
  input  lui,
  input  auipc,
  input  jal,
  input  branch_true,
  input  b,
  input  jalr,
  input  lw,
  output out_11,
  output [1:0] op_A,
  output op_B,
  output mem_write,
  output mem_read,
  output [1:0] imm_sel,
  output write_back,
  output reg_file,
  output [1:0] PC_sel,
  output flush,
  output jalr_2,
  output [2:0] alu_op_2_1_0
);

  and cond_cheak (flush, branch_true, b);
  or or_1 (op_B, i, s, lui, auipc, jalr, lw);
  or or_2 (imm_sel[0], jal, flush, s, r);
  or or_3 (imm_sel[1], auipc, lui, jal, flush, r);
  or or_4 (reg_file, r, i, jal, lui, auipc, jalr, lw);
  or or_5 (PC_sel[0], jalr, flush);
  or or_6 (PC_sel[1], jal, jalr);
  or or_7 (op_A[0], r, jalr, lui, lw, i, s);
  or or_8 (out_11, s, b);
  or or_9 (op_A[1], lui, auipc);
  ALUop2_1_0 aluop2_1_0_1 (
    .r(r), .I(i), .s(s), .Lui(lui), .Auipc(auipc), .Jal(jal), .Jalr(jalr), .Lw(lw), .out_9(alu_op_2_1_0));

  assign jalr_2 = jalr;
  assign mem_read = lw;
  assign mem_write = s;
  assign write_back = lw;
endmodule

module type_decorder (
  input  [6:0] in_1,
  input  in_2,
  output r,
  output i,
  output s,
  output lui,
  output auipc,
  output jal,
  output branch_true,
  output b,
  output jalr,
  output lw
);

  Comparator #(.width(7)) comparator_1 (.a(in_1), .b(7'b0110011), .eq(r));  // open: gt, lt
  Comparator #(.width(7)) comparator_2 (.a(in_1), .b(7'b0010011), .eq(i));  // open: gt, lt
  Comparator #(.width(7)) comparator_3 (.a(in_1), .b(7'b0100011), .eq(s));  // open: gt, lt
  Comparator #(.width(7)) comparator_4 (.a(in_1), .b(7'b0110111), .eq(lui));  // open: gt, lt
  Comparator #(.width(7)) comparator_5 (.a(in_1), .b(7'b0010111), .eq(auipc));  // open: gt, lt
  Comparator #(.width(7)) comparator_6 (.a(in_1), .b(7'b1101111), .eq(jal));  // open: gt, lt
  Comparator #(.width(7)) comparator_7 (.a(in_1), .b(7'b1100011), .eq(b));  // open: gt, lt
  Comparator #(.width(7)) comparator_8 (.a(in_1), .b(7'b1100111), .eq(jalr));  // open: gt, lt
  Comparator #(.width(7)) comparator_9 (.a(in_1), .b(7'b0000011), .eq(lw));  // open: gt, lt

  assign branch_true = in_2;
endmodule

module signal_controller_and_type_decorder (
  input  [6:0] in_1,
  input  in_2,
  output b___s,
  output [1:0] op_A,
  output op_B,
  output mem_write,
  output mem_read,
  output [1:0] imm_sel,
  output write_back,
  output reg_file,
  output [1:0] PC_sel,
  output flush,
  output JALR,
  output [2:0] alu_op_2_1_0
);

  wire type_decorder_1_auipc, type_decorder_1_b, type_decorder_1_branch_true, type_decorder_1_i,
       type_decorder_1_jal, type_decorder_1_jalr, type_decorder_1_lui, type_decorder_1_lw, type_decorder_1_r,
       type_decorder_1_s;

  type_decorder type_decorder_1 (
    .in_1(in_1), .r(type_decorder_1_r), .i(type_decorder_1_i), .s(type_decorder_1_s),
    .lui(type_decorder_1_lui), .auipc(type_decorder_1_auipc), .jal(type_decorder_1_jal),
    .b(type_decorder_1_b), .jalr(type_decorder_1_jalr), .lw(type_decorder_1_lw),
    .branch_true(type_decorder_1_branch_true), .in_2(in_2));
  signal_controler signal_controler_1 (
    .r(type_decorder_1_r), .i(type_decorder_1_i), .s(type_decorder_1_s), .lui(type_decorder_1_lui),
    .auipc(type_decorder_1_auipc), .jal(type_decorder_1_jal), .b(type_decorder_1_b),
    .jalr(type_decorder_1_jalr), .lw(type_decorder_1_lw), .op_A(op_A), .op_B(op_B), .mem_write(mem_write),
    .mem_read(mem_read), .imm_sel(imm_sel), .write_back(write_back), .reg_file(reg_file), .PC_sel(PC_sel),
    .alu_op_2_1_0(alu_op_2_1_0), .branch_true(type_decorder_1_branch_true), .jalr_2(JALR), .out_11(b___s),
    .flush(flush));
endmodule

module alu (
  input  [31:0] a,
  input  [31:0] b,
  input  [3:0] SELECT,
  output [31:0] out_4
);

  wire [31:0] adder_1_out, and_1_out, comparator_1_lt, comparator_2_lt, or_1_out, shifter_1_out,
       shifter_2_out, shifter_3_out, subtractor_1_out, xor_1_out;

  Adder #(.width(32)) adder_1 (.a(a), .b(b), .out(adder_1_out), .cin(1'b0));  // open: cout
  Subtractor #(.width(32)) subtractor_1 (.a(a), .b(b), .out(subtractor_1_out), .bin(1'b0));  // open: bout
  assign and_1_out = a & b;  // AND_Gate and_1, 32 bits wide
  assign or_1_out = a | b;  // OR_Gate or_1, 32 bits wide
  assign xor_1_out = a ^ b;  // XOR_Gate xor_1, 32 bits wide
  Shifter #(.width(32)) shifter_1 (.in(a), .\dist (b[4:0]), .out(shifter_1_out));
  Shifter #(.width(32), .shift("lr")) shifter_2 (.in(a), .\dist (b[4:0]), .out(shifter_2_out));
  Shifter #(.width(32), .shift("ar")) shifter_3 (.in(a), .\dist (b[4:0]), .out(shifter_3_out));
  Comparator #(.width(32)) comparator_1 (.a(a), .b(b), .lt(comparator_1_lt[0]));  // open: gt, eq
  Comparator #(.width(32), .mode("unsigned")) comparator_2 (.a(a), .b(b), .lt(comparator_2_lt[0]));  // open: gt, eq
  Multiplexer #(.select(4), .width(32)) multiplexer_1 (
    .in0(adder_1_out), .in1(subtractor_1_out), .in2(and_1_out), .in3(or_1_out), .in4(xor_1_out),
    .in5(shifter_2_out), .in6(shifter_3_out), .in7(shifter_1_out), .in8(comparator_1_lt),
    .in9(comparator_2_lt), .in14(b), .in15(a), .out(out_4), .sel(SELECT));  // open: in10, in11, in12, in13, en
endmodule

// FETCH
module ALL (
  input  reset,
  output [31:0] out_2,
  output b___s,
  output [1:0] op_A,
  output mem_write,
  output mem_read,
  output write_back,
  output JALR,
  output [31:0] b_out,
  output [1:0] out_10,
  output [31:0] out_11,
  output [4:0] out_12,
  output [31:0] out_13,
  output [31:0] out_14,
  output [4:0] out_15,
  output [31:0] out_16,
  output [31:0] out_17,
  output [31:0] out_18
);

  wire branch_alu_1_out_4, clock, or_1_out, register_2_q, register_3_q,
       signal_controller_and_type_decorder_1_b___s, signal_controller_and_type_decorder_1_flush,
       signal_controller_and_type_decorder_1_jalr, signal_controller_and_type_decorder_1_mem_read,
       signal_controller_and_type_decorder_1_mem_write, signal_controller_and_type_decorder_1_op_b,
       signal_controller_and_type_decorder_1_reg_file, signal_controller_and_type_decorder_1_write_back,
       stage_2_1_out_29, stage_2_1_out_32, stage_2_stalling_1_out_6, stage_2_stalling_1_out_8,
       stage_3_1_out_10, stage_3_1_out_11, stage_3_1_out_12, stage_3_1_out_13, stage_3_1_out_14,
       stage_4_1_out_8, stage_4_1_out_9, stage_4_1_out_10;
  wire [1:0] signal_controller_and_type_decorder_1_imm_sel, signal_controller_and_type_decorder_1_op_a;
  wire [2:0] signal_controller_and_type_decorder_1_alu_op_2_1_0, stage_2_1_out_30, stage_2_1_out_31;
  wire [3:0] alu_controller_1_out_4;
  wire [31:0] adder_1_out, alu_1_out_4, imm_gen_1_i_s_u, imm_gen_1_j, multiplexer_1_out, multiplexer_3_out,
       multiplexer_4_out, multiplexer_5_out, multiplexer_6_out, ram_1_data, register_1_q, rs1, rs2,
       stage_1_1_out_6, stage_1_1_out_7, stage_1_1_out_9, stage_2_1_out_23, stage_2_1_out_25,
       stage_2_1_out_27, stage_2_stalling_1_out_7, stage_3_1_out_15, stage_3_1_out_17, stage_4_1_out_11,
       stage_4_1_out_12, stage_4_1_out_13;

  Multiplexer #(.select(2), .width(32)) multiplexer_1 (
    .in0(adder_1_out), .in1(out_2), .in2(imm_gen_1_j), .in3(out_16), .out(multiplexer_1_out), .sel(out_10));  // open: en
  Register #(.width(32)) register_1 (.D(multiplexer_1_out), .Q(register_1_q), .clk(clock), .clr(reset));  // open: en
  Multiplexer #(.width(32), .enable("false")) multiplexer_2 (
    .in0(register_1_q), .in1(stage_2_stalling_1_out_7), .out(out_14), .sel(stage_2_stalling_1_out_6));
  Adder #(.width(32)) adder_1 (.a(register_1_q), .b(32'h4), .out(adder_1_out), .cin(1'b0));  // open: cout
  Clock u_clock (.out(clock));
  ROM #(.addrWidth(10), .dataWidth(32)) rom_1 (.addr(out_14[11:2]), .data(out_11));  // open: sel
  stage_1 stage_1_1 (
    .in_1(adder_1_out), .in_2(register_1_q), .in_3(out_11), .in_4(out_14), .out_6(stage_1_1_out_6),
    .out_7(stage_1_1_out_7), .out_8(b_out), .out_9(stage_1_1_out_9), .in_5(clock));
  IMM_gen imm_gen_1 (
    .in_1(b_out), .i_s_u(imm_gen_1_i_s_u), .in_2(signal_controller_and_type_decorder_1_imm_sel),
    .mem(stage_1_1_out_9), .j(imm_gen_1_j), .b(out_2));
  signal_controller_and_type_decorder signal_controller_and_type_decorder_1 (
    .in_1(b_out[6:0]), .op_A(signal_controller_and_type_decorder_1_op_a),
    .op_B(signal_controller_and_type_decorder_1_op_b),
    .mem_write(signal_controller_and_type_decorder_1_mem_write),
    .mem_read(signal_controller_and_type_decorder_1_mem_read),
    .imm_sel(signal_controller_and_type_decorder_1_imm_sel),
    .write_back(signal_controller_and_type_decorder_1_write_back),
    .reg_file(signal_controller_and_type_decorder_1_reg_file), .PC_sel(out_10),
    .JALR(signal_controller_and_type_decorder_1_jalr),
    .alu_op_2_1_0(signal_controller_and_type_decorder_1_alu_op_2_1_0), .in_2(branch_alu_1_out_4),
    .b___s(signal_controller_and_type_decorder_1_b___s), .flush(signal_controller_and_type_decorder_1_flush));
  saving_rd saving_rd_1 (.in_1(b_out[11:7]), .out_4(out_15), .in_2(clock), .in_3(register_2_q));
  branch_ALU branch_alu_1 (.rs1(rs1), .rs2(rs2), .bgeu_111(b_out[14:12]), .out_4(branch_alu_1_out_4));
  stage_2_stalling stage_2_stalling_1 (
    .rd(b_out[11:7]), .rs1(b_out[19:15]), .rs2(b_out[24:20]), .clock(clock), .pc(stage_1_1_out_9),
    .out_8(stage_2_stalling_1_out_8), .out_7(stage_2_stalling_1_out_7), .out_6(stage_2_stalling_1_out_6));
  or or_1 (or_1_out, signal_controller_and_type_decorder_1_flush, stage_2_stalling_1_out_8);
  Register #(.width(1)) register_2 (.D(or_1_out), .Q(register_2_q), .clk(clock));  // open: en, clr
  reg_file reg_file_1 (
    .rs1(b_out[19:15]), .rs2(b_out[24:20]), .r_sel(out_15), .rs2__D(rs2), .rs1_D(rs1), .reset(reset),
    .clock(clock), .reg_file_en(signal_controller_and_type_decorder_1_reg_file), .in_1(out_18));
  Register #(.width(1)) register_3 (.D(register_2_q), .Q(register_3_q), .clk(clock));  // open: en, clr
  stage_2 stage_2_1 (
    .in_1(signal_controller_and_type_decorder_1_b___s), .in_2(signal_controller_and_type_decorder_1_op_a),
    .in_3(signal_controller_and_type_decorder_1_mem_write),
    .in_4(signal_controller_and_type_decorder_1_mem_read),
    .in_5(signal_controller_and_type_decorder_1_write_back), .in_6(stage_1_1_out_6),
    .in_7(signal_controller_and_type_decorder_1_jalr), .in_8(stage_1_1_out_7), .in_9(rs1), .in_10(rs2),
    .in_11(imm_gen_1_i_s_u), .in_12(signal_controller_and_type_decorder_1_op_b),
    .in_13(signal_controller_and_type_decorder_1_alu_op_2_1_0), .in_14(b_out[14:12]), .out_18(b___s),
    .out_19(op_A), .out_20(mem_write), .out_21(mem_read), .out_22(write_back), .out_23(stage_2_1_out_23),
    .out_24(JALR), .out_25(stage_2_1_out_25), .out_26(out_13), .out_27(stage_2_1_out_27), .out_28(out_17),
    .out_29(stage_2_1_out_29), .out_30(stage_2_1_out_30), .out_31(stage_2_1_out_31), .in_16(clock),
    .out_32(stage_2_1_out_32), .in_15(b_out[30]), .in_17(register_3_q));
  Multiplexer #(.select(2), .width(32), .enable("false")) multiplexer_3 (
    .in0(stage_2_1_out_23), .in1(out_13), .in2(stage_2_1_out_25), .out(multiplexer_3_out), .sel(op_A));  // open: in3
  Multiplexer #(.width(32)) multiplexer_4 (
    .in0(stage_2_1_out_27), .in1(out_17), .out(multiplexer_4_out), .sel(stage_2_1_out_29));  // open: en
  alu_controller alu_controller_1 (
    .func7(stage_2_1_out_32), .out_4(alu_controller_1_out_4), .aluop_2_1_0(stage_2_1_out_30),
    .func_2_1_0(stage_2_1_out_31));
  alu alu_1 (.a(multiplexer_3_out), .b(multiplexer_4_out), .SELECT(alu_controller_1_out_4), .out_4(alu_1_out_4));
  stage_3 stage_3_1 (
    .in_1(b___s), .in_2(mem_write), .in_3(mem_read), .in_4(write_back), .in_5(JALR), .in_6(stage_2_1_out_23),
    .in_7(alu_1_out_4), .in_8(stage_2_1_out_27), .out_10(stage_3_1_out_10), .out_11(stage_3_1_out_11),
    .out_12(stage_3_1_out_12), .out_13(stage_3_1_out_13), .out_14(stage_3_1_out_14),
    .out_15(stage_3_1_out_15), .out_16(out_16), .out_17(stage_3_1_out_17), .in_9(clock));
  RAM #(.addrWidth(10), .dataWidth(32), .bus("separate")) ram_1 (
    .addr(out_16[11:2]), .din(stage_3_1_out_17), .data(ram_1_data), .str(stage_3_1_out_11), .clk(clock),
    .ld(stage_3_1_out_12));  // open: sel, clr
  stage_4 stage_4_1 (
    .in_1(stage_3_1_out_10), .in_2(stage_3_1_out_13), .in_3(stage_3_1_out_14), .in_4(stage_3_1_out_15),
    .in_5(ram_1_data), .in_6(out_16), .out_8(stage_4_1_out_8), .out_9(stage_4_1_out_9),
    .out_10(stage_4_1_out_10), .out_11(stage_4_1_out_11), .out_12(stage_4_1_out_12),
    .out_13(stage_4_1_out_13), .in_7(clock));
  Multiplexer #(.width(32), .enable("false")) multiplexer_5 (
    .in0(multiplexer_6_out), .in1(stage_4_1_out_11), .out(multiplexer_5_out), .sel(stage_4_1_out_10));
  Multiplexer #(.width(32), .enable("false")) multiplexer_6 (
    .in0(stage_4_1_out_13), .in1(stage_4_1_out_12), .out(multiplexer_6_out), .sel(stage_4_1_out_9));
  Multiplexer #(.width(32), .enable("false")) multiplexer_7 (
    .in0(multiplexer_5_out), .out(out_18), .sel(stage_4_1_out_8));  // open: in1

  assign out_12 = b_out[19:15];

  // Other names for the same wires on the sheet: rd[4:0] = b_out[11:7]; rs15[4:0] = b_out[19:15];
  //   rs25[4:0] = b_out[24:20]

  // Notes on the sheet:
  //   01 B
  //   10 JAL
  //   11 JALR
  //   pc sel
  //   Stage 1
  //   fetch
  //   contents of rom_1 (hex, n*v repeats v):
  //   1663 100513 150593
  //   imm sel
  //   i/s/u
  //   JAL
  //   BRANCH
  //   pc
  //   enable of data hazard
  //   Stage 2
  //   op A
  //   op B
  //   MEM write
  //   pc sel
  //   jalr
  //   alo op
  //   func 3
  //   data hazard intrupt
  //   decorde
  //   MEM read
  //   IMM sel
  //   write back
  //   reg file en
  //   branch  hazard
  //   pc of data hazard
  //   rs1
  //   rs2
  //   rsel
  //   pc + 4
  //   rs1
  //   imm
  //   op A
  //   RS2
  //   op B
  //   Stage 3
  //   execute 
  //   alu func
  //   Stage 4
  //   memory
  //   wb sel
  //   Stage 5
  //   pc+4
  //   JALR 
  //   write back
  //   rd
  //   b/s
endmodule

module IMM_gen (
  input  [31:0] in_1,
  input  [1:0] in_2,
  input  [31:0] mem,
  output [31:0] i_s_u,
  output [31:0] j,
  output [31:0] b
);

  wire [19:0] bit_extender_1_out;
  wire [31:0] shifter_1_out;

  assign bit_extender_1_out = {{19{in_1[31]}}, in_1[31]};  // Bit_Extender bit_extender_1
  Shifter #(.width(32)) shifter_1 (
    .in({bit_extender_1_out[11:0], in_1[31:12]}), .\dist (5'b01100), .out(shifter_1_out));
  Multiplexer #(.select(2), .width(32)) multiplexer_1 (
    .in0({bit_extender_1_out, in_1[31:20]}), .in1({bit_extender_1_out, in_1[31:25], in_1[11:7]}),
    .in2(shifter_1_out), .out(i_s_u), .sel(in_2));  // open: in3, en
  Adder #(.width(32)) adder_1 (
    .a({bit_extender_1_out[10:0], in_1[31], in_1[19:12], in_1[20], in_1[30:21], 1'b0}), .b(mem), .out(j),
    .cin(1'b0));  // open: cout
  Adder #(.width(32)) adder_2 (
    .a({bit_extender_1_out[18:0], in_1[31], in_1[7], in_1[30:25], in_1[11:8], 1'b0}), .b(mem), .out(b),
    .cin(1'b0));  // open: cout
endmodule

module reg_file (
  input  [31:0] in_1,
  input  [4:0] rs1,
  input  [4:0] rs2,
  input  reg_file_en,
  input  [4:0] r_sel,
  input  reset,
  input  clock,
  output [31:0] rs1_D,
  output [31:0] rs2__D
);

  wire decoder_1_out0, decoder_1_out1, decoder_1_out2, decoder_1_out3, decoder_1_out4, decoder_1_out5,
       decoder_1_out6, decoder_1_out7, decoder_1_out8, decoder_1_out9, decoder_1_out10, decoder_1_out11,
       decoder_1_out12, decoder_1_out13, decoder_1_out14, decoder_1_out15, decoder_1_out16, decoder_1_out17,
       decoder_1_out18, decoder_1_out19, decoder_1_out20, decoder_1_out21, decoder_1_out22, decoder_1_out23,
       decoder_1_out24, decoder_1_out25, decoder_1_out26, decoder_1_out27, decoder_1_out28, decoder_1_out29,
       decoder_1_out30, decoder_1_out31;
  wire [31:0] register_1_q, register_2_q, register_3_q, register_4_q, register_5_q, register_6_q,
       register_7_q, register_8_q, register_9_q, register_10_q, register_11_q, register_12_q, register_13_q,
       register_14_q, register_15_q, register_16_q, register_17_q, register_18_q, register_19_q,
       register_20_q, register_21_q, register_22_q, register_23_q, register_24_q, register_25_q,
       register_26_q, register_27_q, register_28_q, register_29_q, register_30_q, register_31_q,
       register_32_q;

  Decoder #(.select(5)) decoder_1 (
    .out0(decoder_1_out0), .out1(decoder_1_out1), .out2(decoder_1_out2), .out3(decoder_1_out3),
    .out4(decoder_1_out4), .out5(decoder_1_out5), .out6(decoder_1_out6), .out7(decoder_1_out7),
    .out8(decoder_1_out8), .out9(decoder_1_out9), .out10(decoder_1_out10), .out11(decoder_1_out11),
    .out12(decoder_1_out12), .out13(decoder_1_out13), .out14(decoder_1_out14), .out15(decoder_1_out15),
    .out16(decoder_1_out16), .out17(decoder_1_out17), .out18(decoder_1_out18), .out19(decoder_1_out19),
    .out20(decoder_1_out20), .out21(decoder_1_out21), .out22(decoder_1_out22), .out23(decoder_1_out23),
    .out24(decoder_1_out24), .out25(decoder_1_out25), .out26(decoder_1_out26), .out27(decoder_1_out27),
    .out28(decoder_1_out28), .out29(decoder_1_out29), .out30(decoder_1_out30), .out31(decoder_1_out31),
    .sel(r_sel), .en(reg_file_en));
  Register #(.width(32)) register_1 (.en(decoder_1_out0), .Q(register_1_q), .clk(clock), .clr(reset));  // open: D
  Register #(.width(32)) register_2 (.D(in_1), .en(decoder_1_out1), .Q(register_2_q), .clk(clock), .clr(reset));
  Register #(.width(32)) register_3 (.D(in_1), .en(decoder_1_out2), .Q(register_3_q), .clk(clock), .clr(reset));
  Register #(.width(32)) register_4 (.D(in_1), .en(decoder_1_out3), .Q(register_4_q), .clk(clock), .clr(reset));
  Register #(.width(32)) register_5 (.D(in_1), .en(decoder_1_out4), .Q(register_5_q), .clk(clock), .clr(reset));
  Register #(.width(32)) register_6 (.D(in_1), .en(decoder_1_out5), .Q(register_6_q), .clk(clock), .clr(reset));
  Register #(.width(32)) register_7 (.D(in_1), .en(decoder_1_out6), .Q(register_7_q), .clk(clock), .clr(reset));
  Register #(.width(32)) register_8 (.D(in_1), .en(decoder_1_out7), .Q(register_8_q), .clk(clock), .clr(reset));
  Register #(.width(32)) register_9 (.D(in_1), .en(decoder_1_out8), .Q(register_9_q), .clk(clock), .clr(reset));
  Register #(.width(32)) register_10 (.D(in_1), .en(decoder_1_out9), .Q(register_10_q), .clk(clock), .clr(reset));
  Register #(.width(32)) register_11 (.D(in_1), .en(decoder_1_out10), .Q(register_11_q), .clk(clock), .clr(reset));
  Register #(.width(32)) register_12 (.D(in_1), .en(decoder_1_out11), .Q(register_12_q), .clk(clock), .clr(reset));
  Register #(.width(32)) register_13 (.D(in_1), .en(decoder_1_out12), .Q(register_13_q), .clk(clock), .clr(reset));
  Register #(.width(32)) register_14 (.D(in_1), .en(decoder_1_out13), .Q(register_14_q), .clk(clock), .clr(reset));
  Register #(.width(32)) register_15 (.D(in_1), .en(decoder_1_out14), .Q(register_15_q), .clk(clock), .clr(reset));
  Register #(.width(32)) register_16 (.D(in_1), .en(decoder_1_out15), .Q(register_16_q), .clk(clock), .clr(reset));
  Register #(.width(32)) register_17 (.D(in_1), .en(decoder_1_out16), .Q(register_17_q), .clk(clock), .clr(reset));
  Register #(.width(32)) register_18 (.D(in_1), .en(decoder_1_out17), .Q(register_18_q), .clk(clock), .clr(reset));
  Register #(.width(32)) register_19 (.D(in_1), .en(decoder_1_out18), .Q(register_19_q), .clk(clock), .clr(reset));
  Register #(.width(32)) register_20 (.D(in_1), .en(decoder_1_out19), .Q(register_20_q), .clk(clock), .clr(reset));
  Register #(.width(32)) register_21 (.D(in_1), .en(decoder_1_out20), .Q(register_21_q), .clk(clock), .clr(reset));
  Register #(.width(32)) register_22 (.D(in_1), .en(decoder_1_out21), .Q(register_22_q), .clk(clock), .clr(reset));
  Register #(.width(32)) register_23 (.D(in_1), .en(decoder_1_out22), .Q(register_23_q), .clk(clock), .clr(reset));
  Register #(.width(32)) register_24 (.D(in_1), .en(decoder_1_out23), .Q(register_24_q), .clk(clock), .clr(reset));
  Register #(.width(32)) register_25 (.D(in_1), .en(decoder_1_out24), .Q(register_25_q), .clk(clock), .clr(reset));
  Register #(.width(32)) register_26 (.D(in_1), .en(decoder_1_out25), .Q(register_26_q), .clk(clock), .clr(reset));
  Register #(.width(32)) register_27 (.D(in_1), .en(decoder_1_out26), .Q(register_27_q), .clk(clock), .clr(reset));
  Register #(.width(32)) register_28 (.D(in_1), .en(decoder_1_out27), .Q(register_28_q), .clk(clock), .clr(reset));
  Register #(.width(32)) register_29 (.D(in_1), .en(decoder_1_out28), .Q(register_29_q), .clk(clock), .clr(reset));
  Register #(.width(32)) register_30 (.D(in_1), .en(decoder_1_out29), .Q(register_30_q), .clk(clock), .clr(reset));
  Register #(.width(32)) register_31 (.D(in_1), .en(decoder_1_out30), .Q(register_31_q), .clk(clock), .clr(reset));
  Register #(.width(32)) register_32 (.D(in_1), .en(decoder_1_out31), .Q(register_32_q), .clk(clock), .clr(reset));
  Multiplexer #(.select(5), .width(32), .enable("false")) multiplexer_1 (
    .in0(register_1_q), .in1(register_2_q), .in2(register_3_q), .in3(register_4_q), .in4(register_5_q),
    .in5(register_6_q), .in6(register_7_q), .in7(register_8_q), .in8(register_9_q), .in9(register_10_q),
    .in10(register_11_q), .in11(register_12_q), .in12(register_13_q), .in13(register_14_q),
    .in14(register_15_q), .in15(register_16_q), .in16(register_17_q), .in17(register_18_q),
    .in18(register_19_q), .in19(register_20_q), .in20(register_21_q), .in21(register_22_q),
    .in22(register_23_q), .in23(register_24_q), .in24(register_25_q), .in25(register_26_q),
    .in26(register_27_q), .in27(register_28_q), .in28(register_29_q), .in29(register_30_q),
    .in30(register_31_q), .in31(register_32_q), .out(rs1_D), .sel(rs1));
  Multiplexer #(.select(5), .width(32), .enable("false")) multiplexer_2 (
    .in0(register_1_q), .in1(register_2_q), .in2(register_3_q), .in3(register_4_q), .in4(register_5_q),
    .in5(register_6_q), .in6(register_7_q), .in7(register_8_q), .in8(register_9_q), .in9(register_10_q),
    .in10(register_11_q), .in11(register_12_q), .in12(register_13_q), .in13(register_14_q),
    .in14(register_15_q), .in15(register_16_q), .in16(register_17_q), .in17(register_18_q),
    .in18(register_19_q), .in19(register_20_q), .in20(register_21_q), .in21(register_22_q),
    .in22(register_23_q), .in23(register_24_q), .in24(register_25_q), .in25(register_26_q),
    .in26(register_27_q), .in27(register_28_q), .in28(register_29_q), .in29(register_30_q),
    .in30(register_31_q), .in31(register_32_q), .out(rs2__D), .sel(rs2));
endmodule

module alu_controller (
  input  [2:0] aluop_2_1_0,
  input  [2:0] func_2_1_0,
  input  func7,
  output [3:0] out_4
);

  wire and_1_out, and_2_out, and_3_out, and_4_out, and_5_out, and_6_out, and_7_out, and_8_out, and_9_out,
       and_10_out, and_11_out, and_12_out, and_13_out, and_14_out, and_15_out, and_16_out, and_17_out,
       and_18_out, and_19_out, and_20_out, not_1_out, not_2_out, not_3_out, not_4_out, not_5_out, not_6_out,
       not_7_out, not_8_out, not_9_out, not_10_out, not_11_out, not_12_out, or_1_out, or_2_out, or_5_out,
       or_7_out, or_8_out, or_9_out;

  not not_1 (not_1_out, aluop_2_1_0[2]);
  not not_2 (not_2_out, aluop_2_1_0[0]);
  not not_3 (not_3_out, func_2_1_0[2]);
  not not_4 (not_4_out, func_2_1_0[1]);
  not not_5 (not_5_out, func_2_1_0[1]);
  not not_6 (not_6_out, func_2_1_0[2]);
  not not_7 (not_7_out, func_2_1_0[1]);
  not not_8 (not_8_out, func_2_1_0[2]);
  not not_9 (not_9_out, func_2_1_0[2]);
  not not_10 (not_10_out, func_2_1_0[1]);
  and and_1 (and_1_out, not_1_out, not_2_out);
  and and_2 (and_2_out, not_3_out, func_2_1_0[1]);
  and and_3 (and_3_out, not_4_out, func_2_1_0[0]);
  and and_4 (and_4_out, func_2_1_0[2], not_5_out);
  and and_5 (and_5_out, not_6_out, not_7_out);
  and and_6 (and_6_out, not_8_out, func7);
  and and_7 (and_7_out, not_9_out, func_2_1_0[0]);
  and and_8 (and_8_out, not_10_out, func_2_1_0[0]);
  not not_11 (not_11_out, func7);
  and and_9 (and_9_out, func_2_1_0[2], func_2_1_0[1]);
  not not_12 (not_12_out, func_2_1_0[0]);
  and and_10 (and_10_out, aluop_2_1_0[2], aluop_2_1_0[1]);
  and and_11 (and_11_out, and_1_out, and_2_out);
  and and_12 (and_12_out, aluop_2_1_0[2], aluop_2_1_0[1]);
  or or_1 (or_1_out, and_3_out, and_4_out);
  and and_13 (and_13_out, aluop_2_1_0[2], aluop_2_1_0[1]);
  and and_14 (and_14_out, and_5_out, func_2_1_0[0]);
  and and_15 (and_15_out, func_2_1_0[2], func7);
  and and_16 (and_16_out, func_2_1_0[2], func_2_1_0[1]);
  and and_17 (and_17_out, aluop_2_1_0[2], aluop_2_1_0[1]);
  or or_2 (or_2_out, and_6_out, and_7_out);
  and and_18 (and_18_out, and_8_out, not_11_out);
  and and_19 (and_19_out, and_9_out, not_12_out);
  and and_20 (and_20_out, and_10_out, aluop_2_1_0[0]);
  or or_3 (out_4[3], and_11_out, and_12_out);
  or or_4 (out_4[2], or_1_out, and_13_out);
  or or_5 (or_5_out, and_14_out, and_15_out);
  or or_6 (out_4[1], or_5_out, or_7_out);
  or or_7 (or_7_out, and_16_out, and_17_out);
  or or_8 (or_8_out, or_2_out, and_18_out);
  or or_9 (or_9_out, and_19_out, and_20_out);
  or or_10 (out_4[0], or_8_out, or_9_out);
endmodule

module branch_ALU (
  input  [31:0] rs1,
  input  [31:0] rs2,
  input  [2:0] bgeu_111,
  output out_4
);

  wire comparator_1_eq, comparator_1_gt, comparator_1_lt, comparator_2_eq, comparator_2_gt, comparator_2_lt,
       not_1_out, or_1_out, or_2_out;

  Comparator #(.width(32)) comparator_1 (
    .a(rs1), .b(rs2), .gt(comparator_1_gt), .eq(comparator_1_eq), .lt(comparator_1_lt));
  or or_1 (or_1_out, comparator_1_gt, comparator_1_eq);
  Comparator #(.width(32)) comparator_2 (
    .a(rs1), .b(rs2), .gt(comparator_2_gt), .eq(comparator_2_eq), .lt(comparator_2_lt));
  or or_2 (or_2_out, comparator_2_eq, comparator_2_gt);
  not not_1 (not_1_out, comparator_1_eq);
  Multiplexer #(.select(3), .disabled(0), .enable("false")) multiplexer_1 (
    .in0(comparator_1_eq), .in1(not_1_out), .in4(comparator_1_lt), .in5(or_1_out), .in6(comparator_2_lt),
    .in7(or_2_out), .out(out_4), .sel(bgeu_111));  // open: in2, in3

  // Notes on the sheet:
  //   beq 000
  //   bne 001
  //   blt 100
  //   bge 101
  //   bltu 110
endmodule

module ALUop2_1_0 (
  input  r,
  input  I,
  input  s,
  input  Lui,
  input  Auipc,
  input  Jal,
  input  Jalr,
  input  Lw,
  output [2:0] out_9
);

  wire nand_1_out, nand_2_out, nand_3_out, nand_4_out, nand_5_out, nand_6_out, nand_7_out, nand_8_out,
       nand_9_out, nand_10_out, nand_11_out, nand_12_out, nand_13_out, nand_14_out, nand_15_out, nand_16_out,
       nand_17_out, nand_18_out, nand_19_out, nand_20_out, nand_21_out, nand_22_out, nand_23_out,
       nand_24_out, nand_25_out, nand_26_out, nand_27_out;

  nand nand_1 (nand_1_out, r, r);
  nand nand_2 (nand_2_out, I, I);
  nand nand_3 (nand_3_out, Jalr, Jalr);
  nand nand_4 (nand_4_out, Lw, Lw);
  nand nand_5 (nand_5_out, r, r);
  nand nand_6 (nand_6_out, s, s);
  nand nand_7 (nand_7_out, Auipc, Auipc);
  nand nand_8 (nand_8_out, Lw, Lw);
  nand nand_9 (nand_9_out, r, r);
  nand nand_10 (nand_10_out, I, I);
  nand nand_11 (nand_11_out, s, s);
  nand nand_12 (nand_12_out, Lui, Lui);
  nand nand_13 (nand_13_out, nand_1_out, nand_2_out);
  nand nand_14 (nand_14_out, nand_3_out, nand_4_out);
  nand nand_15 (nand_15_out, nand_5_out, nand_6_out);
  nand nand_16 (nand_16_out, nand_7_out, nand_8_out);
  nand nand_17 (nand_17_out, nand_9_out, nand_10_out);
  nand nand_18 (nand_18_out, nand_11_out, nand_12_out);
  nand nand_19 (nand_19_out, nand_13_out, nand_13_out);
  nand nand_20 (nand_20_out, nand_14_out, nand_14_out);
  nand nand_21 (nand_21_out, nand_15_out, nand_15_out);
  nand nand_22 (nand_22_out, nand_16_out, nand_16_out);
  nand nand_23 (nand_23_out, nand_17_out, nand_17_out);
  nand nand_24 (nand_24_out, nand_18_out, nand_18_out);
  nand nand_25 (nand_25_out, nand_19_out, nand_20_out);
  nand nand_26 (nand_26_out, nand_21_out, nand_22_out);
  nand nand_27 (nand_27_out, nand_23_out, nand_24_out);
  nand nand_28 (out_9[2], nand_25_out, nand_25_out);
  nand nand_29 (out_9[1], nand_26_out, nand_26_out);
  nand nand_30 (out_9[0], nand_27_out, nand_27_out);
endmodule

module stage_1 (
  input  [31:0] in_1,
  input  [31:0] in_2,
  input  [31:0] in_3,
  input  [31:0] in_4,
  input  in_5,
  output [31:0] out_6,
  output [31:0] out_7,
  output [31:0] out_8,
  output [31:0] out_9
);

  Register #(.width(32)) register_1 (.D(in_1), .Q(out_6), .clk(in_5));  // open: en, clr
  Register #(.width(32)) register_2 (.D(in_2), .Q(out_7), .clk(in_5));  // open: en, clr
  Register #(.width(32)) register_3 (.D(in_3), .Q(out_8), .clk(in_5));  // open: en, clr
  Register #(.width(32)) register_4 (.D(in_4), .Q(out_9), .clk(in_5));  // open: en, clr
endmodule

module stage_2 (
  input  in_1,
  input  [1:0] in_2,
  input  in_3,
  input  in_4,
  input  in_5,
  input  [31:0] in_6,
  input  in_7,
  input  [31:0] in_8,
  input  [31:0] in_9,
  input  [31:0] in_10,
  input  [31:0] in_11,
  input  in_12,
  input  [2:0] in_13,
  input  [2:0] in_14,
  input  in_15,
  input  in_16,
  input  in_17,
  output out_18,
  output [1:0] out_19,
  output out_20,
  output out_21,
  output out_22,
  output [31:0] out_23,
  output out_24,
  output [31:0] out_25,
  output [31:0] out_26,
  output [31:0] out_27,
  output [31:0] out_28,
  output out_29,
  output [2:0] out_30,
  output [2:0] out_31,
  output out_32
);

  Register #(.width(1)) register_1 (.D(in_1), .Q(out_18), .clk(in_16), .clr(in_17));  // open: en
  Register #(.width(2)) register_2 (.D(in_2), .Q(out_19), .clk(in_16), .clr(in_17));  // open: en
  Register #(.width(1)) register_3 (.D(in_3), .Q(out_20), .clk(in_16), .clr(in_17));  // open: en
  Register #(.width(1)) register_4 (.D(in_4), .Q(out_21), .clk(in_16), .clr(in_17));  // open: en
  Register #(.width(1)) register_5 (.D(in_5), .Q(out_22), .clk(in_16), .clr(in_17));  // open: en
  Register #(.width(32)) register_6 (.D(in_6), .Q(out_23), .clk(in_16), .clr(in_17));  // open: en
  Register #(.width(1)) register_7 (.D(in_7), .Q(out_24), .clk(in_16), .clr(in_17));  // open: en
  Register #(.width(32)) register_8 (.D(in_8), .Q(out_25), .clk(in_16), .clr(in_17));  // open: en
  Register #(.width(32)) register_9 (.D(in_9), .Q(out_26), .clk(in_16), .clr(in_17));  // open: en
  Register #(.width(32)) register_10 (.D(in_10), .Q(out_27), .clk(in_16), .clr(in_17));  // open: en
  Register #(.width(32)) register_11 (.D(in_11), .Q(out_28), .clk(in_16), .clr(in_17));  // open: en
  Register #(.width(1)) register_12 (.D(in_12), .Q(out_29), .clk(in_16), .clr(in_17));  // open: en
  Register #(.width(3)) register_13 (.D(in_13), .Q(out_30), .clk(in_16), .clr(in_17));  // open: en
  Register #(.width(3)) register_14 (.D(in_14), .Q(out_31), .clk(in_16), .clr(in_17));  // open: en
  Register #(.width(1)) register_15 (.D(in_15), .Q(out_32), .clk(in_16), .clr(in_17));  // open: en
endmodule

module stage_3 (
  input  in_1,
  input  in_2,
  input  in_3,
  input  in_4,
  input  in_5,
  input  [31:0] in_6,
  input  [31:0] in_7,
  input  [31:0] in_8,
  input  in_9,
  output out_10,
  output out_11,
  output out_12,
  output out_13,
  output out_14,
  output [31:0] out_15,
  output [31:0] out_16,
  output [31:0] out_17
);

  Register #(.width(1)) register_1 (.D(in_1), .Q(out_10), .clk(in_9));  // open: en, clr
  Register #(.width(1)) register_2 (.D(in_2), .Q(out_11), .clk(in_9));  // open: en, clr
  Register #(.width(1)) register_3 (.D(in_3), .Q(out_12), .clk(in_9));  // open: en, clr
  Register #(.width(1)) register_4 (.D(in_4), .Q(out_13), .clk(in_9));  // open: en, clr
  Register #(.width(1)) register_5 (.D(in_5), .Q(out_14), .clk(in_9));  // open: en, clr
  Register #(.width(32)) register_6 (.D(in_6), .Q(out_15), .clk(in_9));  // open: en, clr
  Register #(.width(32)) register_7 (.D(in_7), .Q(out_16), .clk(in_9));  // open: en, clr
  Register #(.width(32)) register_8 (.D(in_8), .Q(out_17), .clk(in_9));  // open: en, clr
endmodule

module stage_4 (
  input  in_1,
  input  in_2,
  input  in_3,
  input  [31:0] in_4,
  input  [31:0] in_5,
  input  [31:0] in_6,
  input  in_7,
  output out_8,
  output out_9,
  output out_10,
  output [31:0] out_11,
  output [31:0] out_12,
  output [31:0] out_13
);

  Register #(.width(1)) register_1 (.D(in_1), .Q(out_8), .clk(in_7));  // open: en, clr
  Register #(.width(1)) register_2 (.D(in_2), .Q(out_9), .clk(in_7));  // open: en, clr
  Register #(.width(1)) register_3 (.D(in_3), .Q(out_10), .clk(in_7));  // open: en, clr
  Register #(.width(32)) register_4 (.D(in_4), .Q(out_11), .clk(in_7));  // open: en, clr
  Register #(.width(32)) register_5 (.D(in_5), .Q(out_12), .clk(in_7));  // open: en, clr
  Register #(.width(32)) register_6 (.D(in_6), .Q(out_13), .clk(in_7));  // open: en, clr
endmodule

module stage_2_stalling (
  input  [31:0] pc,
  input  [4:0] rd,
  input  [4:0] rs1,
  input  [4:0] rs2,
  input  clock,
  output out_6,
  output [31:0] out_7,
  output out_8
);

  wire comparator_1_eq, comparator_2_eq, comparator_3_eq, comparator_4_eq, not_1_out, not_2_out, or_1_out,
       or_2_out, or_3_out, register_3_q, register_4_q, register_5_q, register_6_q;
  wire [4:0] multiplexer_1_out, register_2_q;

  Comparator #(.width(32), .mode("unsigned")) comparator_1 (
    .a(pc), .b({32{1'b0}}), .eq(comparator_1_eq));  // open: gt, lt
  Comparator #(.width(5), .mode("unsigned")) comparator_2 (
    .a(rd), .b({5{1'b0}}), .eq(comparator_2_eq));  // open: gt, lt
  Register #(.width(32)) register_1 (.D(pc), .en(out_8), .Q(out_7), .clk(clock), .clr(register_5_q));
  or or_1 (or_1_out, comparator_1_eq, comparator_2_eq);
  Multiplexer #(.width(5), .enable("false")) multiplexer_1 (
    .in0(rd), .in1(5'b00001), .out(multiplexer_1_out), .sel(or_1_out));
  not not_1 (not_1_out, register_6_q);
  Register #(.width(5)) register_2 (
    .D(multiplexer_1_out), .en(not_1_out), .Q(register_2_q), .clk(clock), .clr(register_6_q));
  Comparator #(.width(5), .mode("unsigned")) comparator_3 (
    .a(register_2_q), .b(rs1), .eq(comparator_3_eq));  // open: gt, lt
  Comparator #(.width(5), .mode("unsigned")) comparator_4 (
    .a(register_2_q), .b(rs2), .eq(comparator_4_eq));  // open: gt, lt
  not not_2 (not_2_out, or_1_out);
  or or_2 (or_2_out, comparator_3_eq, comparator_4_eq);
  or or_3 (or_3_out, or_2_out, register_3_q, register_4_q);
  Register #(.width(1)) register_3 (.D(or_2_out), .Q(register_3_q), .clk(clock));  // open: en, clr
  Comparator #(.width(32), .mode("unsigned")) comparator_5 (.a({32{1'b0}}), .b(out_7), .lt(out_6));  // open: gt, eq
  Multiplexer #(.enable("false")) multiplexer_2 (.in0(or_3_out), .in1(not_2_out), .out(out_8), .sel(or_1_out));
  Register #(.width(1)) register_4 (.D(register_3_q), .Q(register_4_q), .clk(clock));  // open: en, clr
  Register #(.width(1)) register_5 (.D(out_6), .Q(register_5_q), .clk(clock));  // open: en, clr
  Register #(.width(1)) register_6 (.D(register_4_q), .Q(register_6_q), .clk(clock));  // open: en, clr
endmodule

module saving_rd (
  input  [4:0] in_1,
  input  in_2,
  input  in_3,
  output [4:0] out_4
);

  wire register_2_q, register_5_q, register_6_q;
  wire [4:0] demultiplexer_1_out0, demultiplexer_1_out1, multiplexer_1_out, register_1_q, register_3_q,
       register_4_q, register_7_q, register_8_q;

  Demultiplexer #(.width(5), .enable("false")) demultiplexer_1 (
    .out0(demultiplexer_1_out0), .out1(demultiplexer_1_out1), .in(in_1), .sel(in_3));
  Register #(.width(5)) register_1 (.D(demultiplexer_1_out1), .Q(register_1_q), .clk(in_2));  // open: en, clr
  Register #(.width(1)) register_2 (.D(in_3), .Q(register_2_q), .clk(in_2));  // open: en, clr
  Register #(.width(5)) register_3 (.D(register_4_q), .Q(register_3_q), .clk(in_2));  // open: en, clr
  Register #(.width(5)) register_4 (.D(register_1_q), .Q(register_4_q), .clk(in_2));  // open: en, clr
  Register #(.width(1)) register_5 (.D(register_2_q), .Q(register_5_q), .clk(in_2));  // open: en, clr
  Register #(.width(1)) register_6 (.D(register_5_q), .Q(register_6_q), .clk(in_2));  // open: en, clr
  Multiplexer #(.width(5), .enable("false")) multiplexer_1 (
    .in0(demultiplexer_1_out0), .in1(register_3_q), .out(multiplexer_1_out), .sel(register_6_q));
  Register #(.width(5)) register_7 (.D(multiplexer_1_out), .Q(register_7_q), .clk(in_2));  // open: en, clr
  Register #(.width(5)) register_8 (.D(register_7_q), .Q(register_8_q), .clk(in_2));  // open: en, clr
  Register #(.width(5)) register_9 (.D(register_8_q), .Q(out_4), .clk(in_2));  // open: en, clr
endmodule
